// Logisim project CPU2.circ as structural Verilog: 7 circuits, main circuit mboard
module mboard (
);

  wire and_1_out, and_2_out, and_3_out, clock_1_out, cpu_1_oe, cpu_1_we;
  wire [7:0] controlled_buffer_2_out, cpu_1_dout, rom_1_data;
  wire [15:0] cpu_1_addr;

  cpu cpu_1 (.CLK(clock_1_out), .DIN(cpu_1_dout), .ADDR(cpu_1_addr), .DOUT(cpu_1_dout), .WE(cpu_1_we), .OE(cpu_1_oe));
  Clock clock_1 (.out(clock_1_out));
  // Probe on cpu_1_dout
  // Probe on cpu_1_addr
  and and_1 (and_1_out, ~cpu_1_addr[14], ~cpu_1_addr[15], cpu_1_oe);  // AND_Gate
  and and_2 (and_2_out, ~cpu_1_addr[14], ~cpu_1_addr[15], cpu_1_we);  // AND_Gate
  assign cpu_1_dout = and_1_out ? controlled_buffer_2_out : 8'bz;  // Controlled_Buffer controlled_buffer_1
  assign controlled_buffer_2_out = and_2_out ? cpu_1_dout : 8'bz;  // Controlled_Buffer controlled_buffer_2
  and and_3 (and_3_out, cpu_1_addr[15], cpu_1_oe);
  assign cpu_1_dout = and_3_out ? rom_1_data : 8'bz;  // Controlled_Buffer controlled_buffer_3
  RAM #(.addrWidth(14), .databus("bidir"), .enables("line")) ram_1 (
    .addr(cpu_1_addr[13:0]), .data(controlled_buffer_2_out));  // open: we, oe, clk
  ROM #(.addrWidth(15)) rom_1 (.addr(cpu_1_addr[14:0]), .data(rom_1_data));

  // Notes on the sheet:
  //   contents of rom_1 (hex, n*v repeats v):
  //   32766*0 80
endmodule

module cpu (
  input  [7:0] DIN,
  input  CLK,
  output [7:0] DOUT,
  output [15:0] ADDR,
  output WE,
  output OE
);

  wire and_1_out, and_2_out, ctrl_1_clko;
  wire [1:0] ctrl_1_sp;
  wire [2:0] ctrl_1_reg_ab, ctrl_1_reg_cd;
  wire [3:0] alu_1_z, ctrl_1_pc;
  wire [5:0] ctrl_1_alu;
  wire [7:0] ctrl_1_irprobe, multiplexer_1_out, regpr_2_out_9, regpr_2_out_10;
  wire [15:0] pc_1_probe, regpr_1_out_6, regpr_2_out_6, sp_1_probe;

  // Probe on ctrl_1_irprobe
  // Probe on multiplexer_1_out
  Multiplexer #(.width(8)) multiplexer_1 (.in1(DIN), .out(multiplexer_1_out), .sel(and_1_out));  // open: in0
  and and_1 (and_1_out, OE, ~WE);  // AND_Gate
  Multiplexer #(.width(8)) multiplexer_2 (.in1(multiplexer_1_out), .out(DOUT), .sel(and_2_out));  // open: in0
  and and_2 (and_2_out, OE, WE);
  ctrl ctrl_1 (
    .Clk(CLK), .DATABUS(multiplexer_1_out), .FLAG(alu_1_z), .PC(ctrl_1_pc), .ALU(ctrl_1_alu),
    .ClkO(ctrl_1_clko), .IRPROBE(ctrl_1_irprobe), .REG_AB(ctrl_1_reg_ab), .REG_CD(ctrl_1_reg_cd),
    .M({OE, WE}), .SP(ctrl_1_sp));
  // Probe on regpr_1_out_6
  // Probe on pc_1_probe
  // Probe on sp_1_probe
  // Probe on regpr_2_out_6
  REGPR regpr_1 (
    .in_2(ctrl_1_reg_cd[2]), .in_3(ctrl_1_reg_cd[1]), .in_4(ctrl_1_reg_cd[0]), .in_1(multiplexer_1_out),
    .in_5(ctrl_1_clko), .out_6(regpr_1_out_6), .out_7(ADDR), .out_8(multiplexer_1_out));  // open: out_9, out_10
  PC pc_1 (
    .PC_OP1(ctrl_1_pc[1]), .PC_OP0(ctrl_1_pc[0]), .DATAIN(multiplexer_1_out), .E8(ctrl_1_pc[2]),
    .E16(ctrl_1_pc[3]), .CLK(ctrl_1_clko), .PROBE(pc_1_probe), .DATAOUT(multiplexer_1_out), .ADDROUT(ADDR));
  SP sp_1 (
    .OP1(ctrl_1_sp[1]), .OP0(ctrl_1_sp[0]), .DATAIN(multiplexer_1_out), .CLK(ctrl_1_clko),
    .DATAOUT(multiplexer_1_out), .PROBE(sp_1_probe), .ADDROUT(ADDR));
  REGPR regpr_2 (
    .in_2(ctrl_1_reg_ab[2]), .in_3(ctrl_1_reg_ab[1]), .in_4(ctrl_1_reg_ab[0]), .in_1(multiplexer_1_out),
    .in_5(ctrl_1_clko), .out_9(regpr_2_out_9), .out_10(regpr_2_out_10), .out_6(regpr_2_out_6), .out_7(ADDR),
    .out_8(multiplexer_1_out));
  ALU alu_1 (
    .A(regpr_2_out_9), .B(regpr_2_out_10), .cin(ctrl_1_alu[5]), .op3(ctrl_1_alu[4]), .op2(ctrl_1_alu[3]),
    .op1(ctrl_1_alu[2]), .op0(ctrl_1_alu[1]), .X(ctrl_1_alu[0]), .O(multiplexer_1_out), .Z(alu_1_z[0]),
    .G(alu_1_z[1]), .E(alu_1_z[2]), .C(alu_1_z[3]));
  // Probe on ADDR
endmodule

module ALU (
  input  [7:0] A,
  input  [7:0] B,
  input  cin,
  input  op3,
  input  op2,
  input  op1,
  input  op0,
  input  X,
  output [7:0] O,
  output Z,
  output G,
  output E,
  output C
);

  wire adder_1_cout, subtractor_1_bout;
  wire [7:0] adder_1_out, and_1_out, demultiplexer_1_out0, demultiplexer_1_out1, demultiplexer_1_out2,
       demultiplexer_1_out3, demultiplexer_1_out4, demultiplexer_1_out5, demultiplexer_1_out6,
       demultiplexer_1_out7, demultiplexer_2_out0, demultiplexer_2_out1, demultiplexer_2_out2,
       demultiplexer_2_out3, demultiplexer_2_out4, demultiplexer_2_out6, demultiplexer_2_out7, not_1_out,
       or_1_out, shifter_1_out, shifter_2_out, subtractor_1_out, xor_1_out;

  Demultiplexer #(.select(3), .width(8)) demultiplexer_1 (
    .out0(demultiplexer_1_out0), .out1(demultiplexer_1_out1), .out2(demultiplexer_1_out2),
    .out3(demultiplexer_1_out3), .out4(demultiplexer_1_out4), .out5(demultiplexer_1_out5),
    .out6(demultiplexer_1_out6), .out7(demultiplexer_1_out7), .in(A), .sel({op2, op1, op0}));
  Demultiplexer #(.select(3), .width(8)) demultiplexer_2 (
    .out0(demultiplexer_2_out0), .out1(demultiplexer_2_out1), .out2(demultiplexer_2_out2),
    .out3(demultiplexer_2_out3), .out4(demultiplexer_2_out4), .out6(demultiplexer_2_out6),
    .out7(demultiplexer_2_out7), .in(B), .sel({op2, op1, op0}));  // open: out5
  Adder adder_1 (.a(demultiplexer_1_out0), .b(demultiplexer_2_out0), .out(adder_1_out), .cin(cin), .cout(adder_1_cout));
  Subtractor subtractor_1 (
    .a(demultiplexer_1_out1), .b(demultiplexer_2_out1), .out(subtractor_1_out), .bin(cin),
    .bout(subtractor_1_bout));
  assign and_1_out = demultiplexer_1_out2 & demultiplexer_2_out2;  // AND_Gate and_1, 8 bits wide
  assign or_1_out = demultiplexer_1_out3 | demultiplexer_2_out3;  // OR_Gate or_1, 8 bits wide
  assign xor_1_out = demultiplexer_1_out4 ^ demultiplexer_2_out4;  // XOR_Gate xor_1, 8 bits wide
  assign not_1_out = ~demultiplexer_1_out5;  // NOT_Gate not_1, 8 bits wide
  Shifter #(.shift("rl")) shifter_1 (
    .in(demultiplexer_1_out6), .\dist (demultiplexer_2_out6[2:0]), .out(shifter_1_out));
  Shifter #(.shift("rr")) shifter_2 (
    .in(demultiplexer_1_out7), .\dist (demultiplexer_2_out7[2:0]), .out(shifter_2_out));
  Multiplexer #(.disabled("Z"), .enable("true"), .select(3), .width(8)) multiplexer_1 (
    .in0(adder_1_out), .in1(subtractor_1_out), .in2(and_1_out), .in3(or_1_out), .in4(xor_1_out),
    .in5(not_1_out), .in6(shifter_1_out), .in7(shifter_2_out), .out(O), .sel({op2, op1, op0}), .en(X));
  nor nor_1 (Z, A[0], A[1], A[2], A[3], A[4], A[5], A[6], A[7]);
  Comparator comparator_1 (.a(A), .b(B), .gt(G), .eq(E));  // open: lt
  or or_2 (C, adder_1_cout, subtractor_1_bout);

  // Notes on the sheet:
  //   A: pull=down
  //   B: pull=down
endmodule

module ctrl (
  input  Clk,
  input  [7:0] DATABUS,
  input  [3:0] FLAG,
  output [2:0] REG_AB,
  output ClkO,
  output [2:0] REG_CD,
  output [1:0] M,
  output [3:0] PC,
  output [7:0] IRPROBE,
  output [1:0] SP,
  output [5:0] ALU
);

  wire pull_resistor_1_node;
  wire [2:0] counter_1_q, rom_1_data;
  wire [3:0] and_1_out, decoder_1_out3, register_2_q;
  wire [11:11] or_1_out;
  wire [31:23] rom_1_data_2;

  Register register_1 (.D(DATABUS), .en(rom_1_data[1]), .Q(IRPROBE), .clk(Clk));  // open: clr
  Pull_Resistor #(.pull(1)) pull_resistor_1 (.node(pull_resistor_1_node));
  Decoder #(.enable("false"), .select(2)) decoder_1 (
    .out0(decoder_1_out3[3]), .out1(decoder_1_out3[2]), .out2(decoder_1_out3[1]), .out3(decoder_1_out3[0]),
    .sel(IRPROBE[1:0]));
  Register #(.width(4)) register_2 (.D(FLAG), .en(rom_1_data[2]), .Q(register_2_q), .clk(Clk));  // open: clr
  Counter #(.max('h7), .trigger("falling"), .width(3)) counter_1 (
    .count(pull_resistor_1_node), .Q(counter_1_q), .up(pull_resistor_1_node), .clk(Clk), .clr(rom_1_data[0]));  // open: load, D, carry
  assign and_1_out = decoder_1_out3 & register_2_q;  // AND_Gate and_1, 4 bits wide
  or or_1 (or_1_out[11], and_1_out[0], and_1_out[1], and_1_out[2], and_1_out[3]);
  ROM #(.addrWidth(12), .dataWidth(32)) rom_1 (
    .addr({or_1_out[11], IRPROBE, counter_1_q}),
    .data({rom_1_data_2, rom_1_data, REG_AB, REG_CD, M, SP, PC, ALU}));
  Pull_Resistor pull_resistor_2 (.node({rom_1_data_2, rom_1_data, REG_AB, REG_CD, M, SP, PC, ALU}));

  assign ClkO = Clk;

  // Notes on the sheet:
  //   Clk: pull=down
  //   contents of rom_1 (hex, n*v repeats v):
  //   202280 100000 6*0 202280 7*0 202280 7*0 202280 7*0 202280 7*0 202280 7*0 202280 7*0 202280 7*0
  //   202280 100000 6*0 202280 7*0 202280 7*0 202280 7*0 202280 7*0 202280 7*0 202280 7*0 202280 7*0
  //   202280 42280 100000 5*0 202280 62280 100000 5*0 202280 a280 100000 5*0 202280 e280 100000 5*0 202280
  //   5e000 100000 5*0 202280 7e000 100000 5*0 202280 ea000 100000 5*0 202280 ee000 100000 5*0 202280 7*0
  //   202280 7*0 202280 7*0 202280 7*0 202280 7*0 202280 7*0 202280 7*0 202280 7*0 202280 7*0 202280 7*0
  //   202280 7*0 202280 7*0 202280 7*0 202280 7*0 202280 7*0 202280 7*0 202280 7*0 202280 7*0 202280 7*0
  //   202280 7*0 202280 7*0 202280 7*0 202280 7*0 202280 7*0 202280 7*0 202280 7*0 202280 7*0 202280 7*0
  //   202280 7*0 202280 7*0 202280 7*0 202280 7*0 202280 7*0 202280 7*0 202280 7*0 202280 7*0 202280 7*0
  //   202280 7*0 202280 7*0 202280 7*0 202280 7*0 202280 7*0 202280 7*0 202280 7*0 202280 7*0 202280 7*0
  //   202280 7*0 202280 7*0 202280 7*0 202280 7*0 202280 7*0 202280 7*0 202280 7*0 202280 7*0 202280 7*0
  //   202280 7*0 202280 7*0 202280 7*0 202280 7*0 202280 7*0 202280 7*0 202280 7*0 202280 7*0 202280 7*0
  //   202280 7*0 202280 7*0 202280 7*0 202280 7*0 202280 7*0 202280 7*0 202280 7*0 202280 7*0 202280 7*0
  //   202280 7*0 202280 7*0 202280 7*0 202280 7*0 202280 7*0 202280 7*0 202280 7*0 202280 7*0 202280 7*0
  //   202280 7*0 202280 7*0 202280 7*0 202280 7*0 202280 7*0 202280 7*0 202280 7*0 202280 7*0 202280 7*0
  //   202280 7*0 202280 7*0 202280 7*0 202280 7*0 202280 7*0 202280 7*0 202280 7*0 202280 7*0 202280 7*0
  //   202280 7*0 202280 7*0 202280 7*0 202280 7*0 202280 7*0 202280 7*0 202280 7*0 202280 7*0 202280 7*0
  //   202280 7*0 202280 7*0 202280 7*0 202280 7*0 202280 7*0 202280 7*0 202280 7*0 202280 7*0 202280 7*0
  //   202280 7*0 202280 7*0 202280 7*0 202280 7*0 202280 7*0 202280 7*0 202280 7*0 202280 7*0 202280 7*0
  //   202280 7*0 202280 7*0 202280 7*0 202280 7*0 202280 7*0 202280 7*0 202280 7*0 202280 7*0 202280 7*0
  //   202280 7*0 202280 7*0 202280 7*0 202280 7*0 202280 7*0 202280 7*0 202280 7*0 202280 7*0 202280 7*0
  //   202280 7*0 202280 7*0 202280 7*0 202280 7*0 202280 7*0 202280 7*0 202280 7*0 202280 7*0 202280 7*0
  //   202280 7*0 202280 7*0 202280 7*0 202280 7*0 202280 7*0 202280 7*0 202280 7*0 202280 7*0 202280 7*0
  //   202280 7*0 202280 7*0 202280 7*0 202280 7*0 202280 7*0 202280 7*0 202280 7*0 202280 7*0 202280 7*0
  //   202280 7*0 202280 7*0 202280 7*0 202280 7*0 202280 7*0 202280 7*0 202280 7*0 202280 7*0 202280 7*0
  //   202280 7*0 202280 7*0 202280 7*0 202280 7*0 202280 7*0 202280 7*0 202280 7*0 202280 7*0 202280 7*0
  //   202280 7*0 202280 7*0 202280 7*0 202280 7*0 202280 7*0 202280 7*0 202280 7*0 202280 7*0 202280 7*0
  //   202280 7*0 202280 7*0 202280 7*0 202280 7*0 202280 7*0 202280 7*0 202280 7*0 202280 7*0 202280 7*0
  //   202280 7*0 202280 7*0 202280 7*0 202280 7*0 202280 7*0 202280 7*0 202280 7*0 202280 7*0 202280 7*0
  //   202280 7*0 202280 7*0 202280 7*0 202280 7*0 202280 7*0 202280 7*0 202280 7*0 202280 7*0 202280 7*0
  //   202280 7*0 202280 7*0 202280 7*0 202280 7*0 202280 7*0 202280
endmodule

module PC (
  input  PC_OP1,
  input  CLK,
  input  [7:0] DATAIN,
  input  E8,
  input  E16,
  input  PC_OP0,
  output [15:0] PROBE,
  output [15:0] ADDROUT,
  output [7:0] DATAOUT
);

  wire and_1_out, and_2_out, counter_1_carry;

  and and_1 (and_1_out, PC_OP1, ~PC_OP0);  // AND_Gate
  and and_2 (and_2_out, ~PC_OP1, PC_OP0);  // AND_Gate
  Counter counter_1 (
    .load(and_2_out), .D(DATAIN), .count(PC_OP1), .Q(PROBE[7:0]), .carry(counter_1_carry), .up(and_1_out),
    .clk(CLK));  // open: clr
  Counter counter_2 (
    .load(and_2_out), .D(PROBE[7:0]), .count(counter_1_carry), .Q(PROBE[15:8]), .up(and_1_out), .clk(CLK));  // open: carry, clr
  assign ADDROUT = E16 ? PROBE : 16'bz;  // Controlled_Buffer controlled_buffer_1
  assign DATAOUT = E8 ? PROBE[15:8] : 8'bz;  // Controlled_Buffer controlled_buffer_2

  // Notes on the sheet:
  //   PROBE: pull=down
endmodule

module SP (
  input  OP1,
  input  OP0,
  input  [7:0] DATAIN,
  input  CLK,
  output [15:0] PROBE,
  output [15:0] ADDROUT,
  output [7:0] DATAOUT
);

  wire and_1_out, and_2_out, and_3_out;

  and and_1 (and_1_out, ~OP1, OP0);  // AND_Gate
  and and_2 (and_2_out, OP1, ~OP0);  // AND_Gate
  and and_3 (and_3_out, OP1, OP0);
  Register register_1 (.D(DATAIN), .en(and_1_out), .Q(PROBE[7:0]), .clk(CLK));  // open: clr
  Register register_2 (.D(PROBE[7:0]), .en(and_1_out), .Q(PROBE[15:8]), .clk(CLK));  // open: clr
  assign DATAOUT = and_2_out ? PROBE[15:8] : 8'bz;  // Controlled_Buffer controlled_buffer_1
  assign ADDROUT = and_3_out ? PROBE : 16'bz;  // Controlled_Buffer controlled_buffer_2
endmodule

module REGPR (
  input  [7:0] in_1,
  input  in_2,
  input  in_3,
  input  in_4,
  input  in_5,
  output [15:0] out_6,
  output [15:0] out_7,
  output [7:0] out_8,
  output [7:0] out_9,
  output [7:0] out_10
);

  wire and_1_out, and_2_out, and_3_out, and_4_out;

  and and_1 (and_1_out, ~in_2, in_3, ~in_4);  // AND_Gate
  and and_2 (and_2_out, ~in_2, in_3, in_4);  // AND_Gate
  and and_3 (and_3_out, in_2, in_3, in_4);
  and and_4 (and_4_out, in_2, ~in_3);  // AND_Gate
  Register register_1 (.D(in_1), .en(and_1_out), .Q(out_6[7:0]), .clk(in_5));  // open: clr
  assign out_7 = and_3_out ? out_6 : 16'bz;  // Controlled_Buffer controlled_buffer_1
  Register register_2 (.D(in_1), .en(and_2_out), .Q(out_6[15:8]), .clk(in_5));  // open: clr
  Multiplexer #(.disabled("Z"), .enable("true"), .width(8)) multiplexer_1 (
    .in0(out_6[7:0]), .in1(out_6[15:8]), .out(out_8), .sel(in_4), .en(and_4_out));

  assign out_9 = out_6[7:0];
  assign out_10 = out_6[15:8];
endmodule
